// Logisim project transis.circ as structural Verilog: 1 circuit, main circuit main
module main (
  input  in_1,
  input  in_2,
  input  in_3,
  input  in_4,
  input  in_5,
  input  in_6
);

  wire transistor_1_out, transistor_2_out, transistor_3_out, transistor_4_out, transistor_5_out,
       transistor_7_out;

  Transistor transistor_1 (.in(1'b0), .out(transistor_1_out), .gate(in_1));
  Transistor transistor_2 (.in(1'b1), .out(transistor_2_out), .gate(in_3));
  Transistor #(.\type ("n")) transistor_3 (.in(1'b0), .out(transistor_3_out), .gate(in_5));
  Transistor #(.\type ("n")) transistor_4 (.in(1'b1), .out(transistor_4_out), .gate(in_6));
  // Probe on transistor_1_out
  // Probe on transistor_2_out
  // Probe on transistor_3_out
  // Probe on transistor_4_out
  Transistor transistor_5 (.in(in_4), .out(transistor_5_out), .gate(in_2));
  Transistor transistor_6 (.in(in_2), .out(transistor_5_out), .gate(in_4));
  Transistor #(.\type ("n")) transistor_7 (.in(in_4), .out(transistor_7_out), .gate(in_2));
  Transistor #(.\type ("n")) transistor_8 (.in(transistor_7_out), .out(transistor_5_out), .gate(in_4));
  // Probe on transistor_5_out
endmodule
