// Logisim project practica2.circ as structural Verilog: 7 circuits, main circuit main
module main (
  input  [2:0] in_1,
  input  [2:0] in_2,
  output [2:0] out_3
);

  assign out_3 = in_1 & in_2;  // AND_Gate and_1, 3 bits wide
endmodule

module primo (
  input  [2:0] \Número_en_binario ,
  output _1_si_es_primo
);

  wire and_1_out, and_2_out, and_3_out, not_1_out;

  not not_1 (not_1_out, \Número_en_binario [2]);
  and and_1 (and_1_out, \Número_en_binario [1], not_1_out);
  and and_2 (and_2_out, \Número_en_binario [1], \Número_en_binario [0]);
  and and_3 (and_3_out, \Número_en_binario [2], \Número_en_binario [0]);
  or or_1 (_1_si_es_primo, and_1_out, and_2_out, and_3_out);

  // Notes on the sheet:
  //   Circuito que decide si un número es primo
endmodule

module Implicacion (
  input  P,
  input  Q
);

  wire transistor_1_out;

  Transistor transistor_1 (.in(1'b1), .out(transistor_1_out), .gate(P));
  Transistor #(.\type ("n")) transistor_2 (.in(Q), .out(transistor_1_out), .gate(P));
  // Probe on transistor_1_out

  // Notes on the sheet:
  //   P -> Q
endmodule

module menor (
  input  [1:0] X,
  input  [1:0] Y,
  output Igual,
  output Menor
);

  wire and_1_out, and_2_out, and_3_out, and_4_out, and_5_out, not_1_out, not_2_out, not_3_out, not_4_out,
       X1_Y1_2_out, X1_Y1_out, X2_Y2_2_out, X2_Y2_out;

  not not_1 (not_1_out, X[0]);
  not not_2 (not_2_out, X[1]);
  not not_3 (not_3_out, Y[0]);
  not not_4 (not_4_out, Y[1]);
  and and_1 (and_1_out, X[0], Y[0]);
  and and_2 (and_2_out, not_1_out, not_3_out);
  and and_3 (and_3_out, X[1], Y[1]);
  and and_4 (and_4_out, not_2_out, not_4_out);
  or X1_Y1 (X1_Y1_out, and_1_out, and_2_out);
  or X2_Y2 (X2_Y2_out, and_3_out, and_4_out);
  and X1_Y1_2 (X1_Y1_2_out, not_1_out, Y[0]);
  and X2_Y2_2 (X2_Y2_2_out, not_2_out, Y[1]);
  and and_5 (and_5_out, X2_Y2_out, X1_Y1_2_out);
  and and_6 (Igual, X1_Y1_out, X2_Y2_out);
  or or_1 (Menor, and_5_out, X2_Y2_2_out);

  // Notes on the sheet:
  //   Comprueba si el número binario X=X2X1 es menor o igual que el Y=Y2Y1
endmodule

module Elevador (
  input  [1:0] \Posición ,
  input  [1:0] Piso_siguiente,
  output [1:0] \Número_de_pisos_a_moverse ,
  output \Dirección 
);

  wire and_1_out, and_2_out, Menor_igual, Menor_menor, not_1_out, not_2_out, not_3_out, not_4_out, XOR_2_s,
       XOR_s;

  not not_1 (not_1_out, \Posición [0]);
  not not_2 (not_2_out, \Posición [1]);
  not not_3 (not_3_out, Piso_siguiente[0]);
  not not_4 (not_4_out, Piso_siguiente[1]);
  and and_1 (and_1_out, \Posición [0], not_2_out, not_3_out, Piso_siguiente[1]);
  and and_2 (and_2_out, not_1_out, \Posición [1], Piso_siguiente[0], not_4_out);
  \xor  XOR (.A(and_1_out), .B(Piso_siguiente[1]), .S(XOR_s));
  \xor  XOR_2 (.A(\Posición [1]), .B(and_2_out), .S(XOR_2_s));
  \xor  XOR_3 (.A(\Posición [0]), .B(Piso_siguiente[0]), .S(\Número_de_pisos_a_moverse [0]));
  \xor  XOR_4 (.A(XOR_s), .B(XOR_2_s), .S(\Número_de_pisos_a_moverse [1]));
  menor Menor (.X(\Posición ), .Y(Piso_siguiente), .Igual(Menor_igual), .Menor(Menor_menor));
  or or_1 (\Dirección , Menor_igual, Menor_menor);

  // Notes on the sheet:
  //   1: Arriba
  //   0: Abajo
endmodule

module \xor  (
  input  A,
  input  B,
  output S
);

  wire and_1_out, and_2_out, not_1_out, not_2_out;

  not not_1 (not_1_out, A);
  not not_2 (not_2_out, B);
  and and_1 (and_1_out, A, not_2_out);
  and and_2 (and_2_out, not_1_out, B);
  or or_1 (S, and_1_out, and_2_out);
endmodule

module NAND (
  input  P,
  input  Q
);

  wire transistor_1_out, transistor_2_out;

  Transistor transistor_1 (.in(1'b1), .out(transistor_1_out), .gate(P));
  Transistor transistor_2 (.in(1'b1), .out(transistor_2_out), .gate(Q));
  Transistor #(.\type ("n")) transistor_3 (.in(1'b0), .out(transistor_2_out), .gate(Q));
  Transistor #(.\type ("n")) transistor_4 (.in(transistor_2_out), .out(transistor_1_out), .gate(P));
  // Probe on transistor_1_out
endmodule
