// Logisim project secuenciales.circ as structural Verilog: 8 circuits, main circuit main
module main (
  input  Entrada,
  output out_2,
  output out_3,
  output out_4,
  output out_5,
  output out_6
);

  wire clock_1_out;

  Clock clock_1 (.out(clock_1_out));
  D_Flip_Flop d_ff_1 (.clk(clock_1_out), .D(out_3), .Q(out_2));  // open: Qn, preset, en, reset
  D_Flip_Flop d_ff_2 (.clk(clock_1_out), .D(out_4), .Q(out_3));  // open: Qn, preset, en, reset
  D_Flip_Flop d_ff_3 (.clk(clock_1_out), .D(out_5), .Q(out_4));  // open: Qn, preset, en, reset
  D_Flip_Flop d_ff_4 (.clk(clock_1_out), .D(out_6), .Q(out_5));  // open: Qn, preset, en, reset
  D_Flip_Flop d_ff_5 (.clk(clock_1_out), .D(Entrada), .Q(out_6));  // open: Qn, preset, en, reset

  // Notes on the sheet:
  //   Circuito de desplazamiento.
endmodule

module cont9 (
  input  Reloj,
  output [3:0] Salida
);

  wire A_qn, and_1_out, and_2_out, and_3_out, and_4_out, C_qn;

  J_K_Flip_Flop A (.J(and_4_out), .clk(Reloj), .K(and_3_out), .Q(Salida[3]), .Qn(A_qn));  // open: preset, en, reset
  and and_1 (and_1_out, A_qn, Salida[0]);
  J_K_Flip_Flop B (.J(and_2_out), .clk(Reloj), .K(and_2_out), .Q(Salida[2]));  // open: Qn, preset, en, reset
  and and_2 (and_2_out, Salida[1], Salida[0]);
  and and_3 (and_3_out, C_qn, Salida[0]);
  J_K_Flip_Flop C (.J(and_1_out), .clk(Reloj), .K(and_2_out), .Q(Salida[1]), .Qn(C_qn));  // open: preset, en, reset
  and and_4 (and_4_out, Salida[2], Salida[1], Salida[0]);
  J_K_Flip_Flop D (.J(1'b1), .clk(Reloj), .K(1'b1), .Q(Salida[0]));  // open: Qn, preset, en, reset

  // Notes on the sheet:
  //   Circuito secuencial que recibe un pulso como entrada y de salida los números de 0 a 9
endmodule

module cont999 (
);

  wire and_1_out, and_2_out, clock_1_out, not_1_out, not_2_out, not_3_out, not_4_out, not_5_out, not_6_out,
       not_7_out, not_8_out;
  wire [3:0] cont9_1_salida, cont9_2_salida, cont9_3_salida;

  cont9 cont9_1 (.Reloj(and_1_out), .Salida(cont9_1_salida));
  Hex_Digit_Display hex_digit_display_1 (.value(cont9_1_salida));  // open: dp
  not not_1 (not_1_out, cont9_2_salida[2]);
  not not_2 (not_2_out, cont9_2_salida[3]);
  cont9 cont9_2 (.Reloj(and_2_out), .Salida(cont9_2_salida));
  Hex_Digit_Display hex_digit_display_2 (.value(cont9_2_salida));  // open: dp
  and and_1 (and_1_out, not_2_out, not_1_out, not_4_out, not_3_out);
  not not_3 (not_3_out, cont9_2_salida[0]);
  not not_4 (not_4_out, cont9_2_salida[1]);
  Hex_Digit_Display hex_digit_display_3 (.value(cont9_3_salida));  // open: dp
  not not_5 (not_5_out, cont9_3_salida[3]);
  cont9 cont9_3 (.Reloj(clock_1_out), .Salida(cont9_3_salida));
  and and_2 (and_2_out, not_5_out, not_6_out, not_7_out, not_8_out);
  not not_6 (not_6_out, cont9_3_salida[2]);
  not not_7 (not_7_out, cont9_3_salida[1]);
  not not_8 (not_8_out, cont9_3_salida[0]);
  Clock clock_1 (.out(clock_1_out));

  // Notes on the sheet:
  //   Circuito que cuenta de 0 a 999
endmodule

module _9display (
);

  wire clock_1_out;
  wire [3:0] cont9_1_salida;

  Clock clock_1 (.out(clock_1_out));
  cont9 cont9_1 (.Reloj(clock_1_out), .Salida(cont9_1_salida));
  Hex_Digit_Display hex_digit_display_1 (.value(cont9_1_salida));  // open: dp
endmodule

module automata (
  input  x,
  output [1:0] Estado
);

  wire A_prime_B_prime_x_prime_out, A_prime_Bx_prime_out, A_qn, AB_prime_out, AB_prime_x_prime_out, Ax_out,
       B_qn, clock_1_out, not_1_out, or_1_out, or_2_out;

  Clock clock_1 (.out(clock_1_out));
  not not_1 (not_1_out, x);
  D_Flip_Flop A (.clk(clock_1_out), .D(or_1_out), .Q(Estado[1]), .Qn(A_qn));  // open: preset, en, reset
  D_Flip_Flop B (.clk(clock_1_out), .D(or_2_out), .Q(Estado[0]), .Qn(B_qn));  // open: preset, en, reset
  and Ax (Ax_out, Estado[1], x);
  and A_prime_Bx_prime (A_prime_Bx_prime_out, A_qn, Estado[0], not_1_out);
  and AB_prime (AB_prime_out, Estado[1], B_qn);
  and A_prime_B_prime_x_prime (A_prime_B_prime_x_prime_out, A_qn, B_qn, not_1_out);
  and AB_prime_x_prime (AB_prime_x_prime_out, Estado[1], B_qn, not_1_out);
  or or_1 (or_1_out, Ax_out, A_prime_Bx_prime_out, AB_prime_out);
  or or_2 (or_2_out, A_prime_B_prime_x_prime_out, AB_prime_x_prime_out);
endmodule

// Registro
module registro (
  input  Reloj,
  input  _1,
  input  _2,
  input  _3,
  input  _4,
  input  _5,
  input  _6,
  input  _7,
  input  _8,
  output _1_2,
  output _2_2,
  output _3_2,
  output _4_2,
  output _5_2,
  output _6_2,
  output _7_2,
  output _8_2
);

  wire not_1_out, not_2_out, not_3_out, not_4_out, not_5_out, not_6_out, not_7_out, not_8_out;

  not not_1 (not_1_out, _1);
  not not_2 (not_2_out, _2);
  not not_3 (not_3_out, _3);
  not not_4 (not_4_out, _4);
  not not_5 (not_5_out, _5);
  not not_6 (not_6_out, _6);
  not not_7 (not_7_out, _7);
  not not_8 (not_8_out, _8);
  S_R_Flip_Flop s_r_ff_1 (.S(_1), .clk(Reloj), .R(not_1_out), .Q(_1_2));  // open: Qn, preset, reset, en
  S_R_Flip_Flop s_r_ff_2 (.S(_2), .clk(Reloj), .R(not_2_out), .Q(_2_2));  // open: Qn, preset, reset, en
  S_R_Flip_Flop s_r_ff_3 (.S(_3), .clk(Reloj), .R(not_3_out), .Q(_3_2));  // open: Qn, preset, reset, en
  S_R_Flip_Flop s_r_ff_4 (.S(_4), .clk(Reloj), .R(not_4_out), .Q(_4_2));  // open: Qn, preset, reset, en
  S_R_Flip_Flop s_r_ff_5 (.S(_5), .clk(Reloj), .R(not_5_out), .Q(_5_2));  // open: Qn, preset, reset, en
  S_R_Flip_Flop s_r_ff_6 (.S(_6), .clk(Reloj), .R(not_6_out), .Q(_6_2));  // open: Qn, preset, reset, en
  S_R_Flip_Flop s_r_ff_7 (.S(_7), .clk(Reloj), .R(not_7_out), .Q(_7_2));  // open: Qn, preset, reset, en
  S_R_Flip_Flop s_r_ff_8 (.S(_8), .clk(Reloj), .R(not_8_out), .Q(_8_2));  // open: Qn, preset, reset, en

  // Notes on the sheet:
  //   Registro de 8 bits
endmodule

module banco (
  input  Escribir,
  input  [7:0] Escribir_datos,
  input  [1:0] Escribir_registro,
  input  [1:0] Leer_registro_1,
  input  [1:0] Leer_registro_2,
  output [7:0] Leer_datos_1,
  output [7:0] Leer_datos_2
);

  wire and_1_out, and_2_out, and_3_out, and_4_out, not_1_out, not_2_out, not_3_out, not_4_out;
  wire [7:0] _0__1_2, _1__1_2, _2__1_2, _3__1_2, demultiplexer_1_out0, demultiplexer_1_out1,
       demultiplexer_1_out2, demultiplexer_1_out3;

  Demultiplexer #(.select(2), .width(8)) demultiplexer_1 (
    .out0(demultiplexer_1_out0), .out1(demultiplexer_1_out1), .out2(demultiplexer_1_out2),
    .out3(demultiplexer_1_out3), .in(Escribir_datos), .sel(Escribir_registro));  // open: en
  not not_1 (not_1_out, Escribir_registro[0]);
  not not_2 (not_2_out, Escribir_registro[1]);
  not not_3 (not_3_out, Escribir_registro[1]);
  and and_1 (and_1_out, Escribir, not_1_out, not_2_out);
  and and_2 (and_2_out, Escribir, Escribir_registro[0], not_3_out);
  not not_4 (not_4_out, Escribir_registro[0]);
  and and_3 (and_3_out, Escribir, not_4_out, Escribir_registro[1]);
  and and_4 (and_4_out, Escribir, Escribir_registro[0], Escribir_registro[1]);
  registro _0 (
    ._1(demultiplexer_1_out0[0]), ._2(demultiplexer_1_out0[1]), ._3(demultiplexer_1_out0[2]),
    ._4(demultiplexer_1_out0[3]), ._5(demultiplexer_1_out0[4]), ._6(demultiplexer_1_out0[5]),
    ._7(demultiplexer_1_out0[6]), ._8(demultiplexer_1_out0[7]), .Reloj(and_1_out), ._1_2(_0__1_2[0]),
    ._2_2(_0__1_2[1]), ._3_2(_0__1_2[2]), ._4_2(_0__1_2[3]), ._5_2(_0__1_2[4]), ._6_2(_0__1_2[5]),
    ._7_2(_0__1_2[6]), ._8_2(_0__1_2[7]));
  registro _1 (
    ._1(demultiplexer_1_out1[0]), ._2(demultiplexer_1_out1[1]), ._3(demultiplexer_1_out1[2]),
    ._4(demultiplexer_1_out1[3]), ._5(demultiplexer_1_out1[4]), ._6(demultiplexer_1_out1[5]),
    ._7(demultiplexer_1_out1[6]), ._8(demultiplexer_1_out1[7]), .Reloj(and_2_out), ._1_2(_1__1_2[0]),
    ._2_2(_1__1_2[1]), ._3_2(_1__1_2[2]), ._4_2(_1__1_2[3]), ._5_2(_1__1_2[4]), ._6_2(_1__1_2[5]),
    ._7_2(_1__1_2[6]), ._8_2(_1__1_2[7]));
  registro _2 (
    ._1(demultiplexer_1_out2[0]), ._2(demultiplexer_1_out2[1]), ._3(demultiplexer_1_out2[2]),
    ._4(demultiplexer_1_out2[3]), ._5(demultiplexer_1_out2[4]), ._6(demultiplexer_1_out2[5]),
    ._7(demultiplexer_1_out2[6]), ._8(demultiplexer_1_out2[7]), .Reloj(and_3_out), ._1_2(_2__1_2[0]),
    ._2_2(_2__1_2[1]), ._3_2(_2__1_2[2]), ._4_2(_2__1_2[3]), ._5_2(_2__1_2[4]), ._6_2(_2__1_2[5]),
    ._7_2(_2__1_2[6]), ._8_2(_2__1_2[7]));
  registro _3 (
    ._1(demultiplexer_1_out3[0]), ._2(demultiplexer_1_out3[1]), ._3(demultiplexer_1_out3[2]),
    ._4(demultiplexer_1_out3[3]), ._5(demultiplexer_1_out3[4]), ._6(demultiplexer_1_out3[5]),
    ._7(demultiplexer_1_out3[6]), ._8(demultiplexer_1_out3[7]), .Reloj(and_4_out), ._1_2(_3__1_2[0]),
    ._2_2(_3__1_2[1]), ._3_2(_3__1_2[2]), ._4_2(_3__1_2[3]), ._5_2(_3__1_2[4]), ._6_2(_3__1_2[5]),
    ._7_2(_3__1_2[6]), ._8_2(_3__1_2[7]));
  Multiplexer #(.select(2), .width(8)) multiplexer_1 (
    .in0(_0__1_2), .in1(_1__1_2), .in2(_2__1_2), .in3(_3__1_2), .out(Leer_datos_1), .sel(Leer_registro_1));  // open: en
  Multiplexer #(.select(2), .width(8)) multiplexer_2 (
    .in0(_0__1_2), .in1(_1__1_2), .in2(_2__1_2), .in3(_3__1_2), .out(Leer_datos_2), .sel(Leer_registro_2));  // open: en

  // Notes on the sheet:
  //   Banco de registros
endmodule

module interconexion (
  input  [2:0] \Código_de_operación ,
  input  Escribir,
  input  [7:0] Escribir_datos,
  input  [1:0] Escribir_registro,
  input  [1:0] Leer_registro_1,
  input  [1:0] Leer_registro_2,
  input  Seleccionar_entrada,
  output [7:0] Resultado,
  output Overflow
);

  wire [7:0] Banco_leer_datos_1, Banco_leer_datos_2, multiplexer_1_out;

  Multiplexer #(.width(8)) multiplexer_1 (
    .in0(Escribir_datos), .in1(Resultado), .out(multiplexer_1_out), .sel(Seleccionar_entrada));  // open: en
  banco Banco (
    .Escribir(Escribir), .Escribir_datos(multiplexer_1_out), .Escribir_registro(Escribir_registro),
    .Leer_registro_1(Leer_registro_1), .Leer_registro_2(Leer_registro_2), .Leer_datos_1(Banco_leer_datos_1),
    .Leer_datos_2(Banco_leer_datos_2));
  ALU5 ALU (
    .A0(Banco_leer_datos_1[0]), .B0(Banco_leer_datos_1[1]), .A1(Banco_leer_datos_1[2]),
    .B1(Banco_leer_datos_1[3]), .A2(Banco_leer_datos_1[4]), .B2(Banco_leer_datos_1[5]),
    .A3(Banco_leer_datos_1[6]), .B3(Banco_leer_datos_1[7]), .A4(Banco_leer_datos_2[0]),
    .B4(Banco_leer_datos_2[1]), .A5(Banco_leer_datos_2[2]), .B5(Banco_leer_datos_2[3]),
    .A6(Banco_leer_datos_2[4]), .B6(Banco_leer_datos_2[5]), .A7(Banco_leer_datos_2[6]),
    .B7(Banco_leer_datos_2[7]), .in_1(\Código_de_operación ), .out_26(Overflow), .S0(Resultado[0]),
    .S1(Resultado[1]), .S2(Resultado[2]), .S3(Resultado[3]), .S4(Resultado[4]), .S5(Resultado[5]),
    .S6(Resultado[6]), .S7(Resultado[7]));

  // Notes on the sheet:
  //   Decidir si se va a escribir lo que salió de la ALU o lo que está en la entrada.
  //   000-AND
  //   001-OR
  //   010-NOR
  //   011-igualdad
  //   100-suma
  //   101-resta
endmodule
